# Fritzing sketch protoboard (saved by Fritzing 1.0.1rc)
circuit board: 7.05256cm x 7.65096cm

parts:
  MotorController = Pololu A4988 [package=SO16]
  Mod2 = Amica NodeMCU DEVKIT 1.0
  LimitClosed1 = Pushbutton [package=THT]
  LimitOpen1 = Pushbutton [package=THT]
  C2 = Electrolytic Capacitor [capacitance=100nF voltage=35V package="100 mil [THT, electrolytic]"]
  HC-SR04_Sensor_1 = HC-SR04 Ultrasonic Distance Sensor
  J-Present = Camdenboss CTB0158-4 [part_number=CTB0158-4 package=THT]
  J-Motor = Camdenboss CTB0158-4 [part_number=CTB0158-4 package=THT]
  J-Closed = Camdenboss CTB0158-2 [part_number=CTB0158-2 package=THT]
  J-Open = Camdenboss CTB0158-2 [part_number=CTB0158-2 package=THT]
  Power_plug1 = Power plug
  Motor = Stepper Motor - Unipolar
  JPower = Camdenboss CTB0158-4 [part_number=CTB0158-4 package=THT]
  S2 = H-Bridge with L298N

nets:
  N1: MotorController.ENABLE, Mod2.pin_14
  N2: MotorController.RESET, MotorController.SLEEP
  N3: MotorController.STEP, Mod2.pin_13
  N4: MotorController.DIR, Mod2.pin_12
  N5: MotorController.GND#8, Mod2.pin2, Mod2.pin_9, Mod2.pin_25, Mod2.pin_29, C2.-, J-Present.pin4, Power_plug1.GND, JPower.pin2
  N6: MotorController.VDD, Mod2.pin1, Mod2.pin_10
  N7: MotorController.1B, J-Motor.pin4
  N8: MotorController.1A, J-Motor.pin3
  N9: MotorController.2A, J-Motor.pin2
  N10: MotorController.2B, J-Motor.pin1
  N11: MotorController.VMOT, C2.+, Power_plug1.VCC, JPower.pin1
  N12: Mod2.pin5, J-Present.pin2
  N13: Mod2.pin6, J-Present.pin3
  N14: Mod2.pin7, J-Closed.pin1
  N15: Mod2.pin8, J-Open.pin1
  N16: Mod2.pin_30, J-Present.pin1, JPower.pin3
  N17: LimitClosed1.leg0, J-Closed.terminal_1
  N18: LimitClosed1.leg1, J-Closed.terminal_2
  N19: LimitOpen1.leg0, J-Open.terminal_1
  N20: LimitOpen1.leg1, J-Open.terminal_2
  N21: HC-SR04_Sensor_1.VCC, J-Present.terminal_1
  N22: HC-SR04_Sensor_1.TRIG, J-Present.terminal_2
  N23: HC-SR04_Sensor_1.ECHO, J-Present.terminal_3
  N24: HC-SR04_Sensor_1.GND, J-Present.terminal_4
  N25: J-Motor.terminal_1, Motor.A
  N26: J-Motor.terminal_2, Motor.C
  N27: J-Motor.terminal_3, Motor.B
  N28: J-Motor.terminal_4, Motor.D
  N29: J-Closed.pin2, J-Open.pin2
  N30: JPower.terminal_1, S2.12V
  N31: JPower.terminal_2, S2.GND
  N32: JPower.terminal_3, S2.5V

custom parts:
  H-Bridge with L298N: h-bridge
